# Fritzing sketch receivercurcuit (saved by Fritzing 0.9.3b)
breadboards: 1

parts:
  Part3 = Arduino Uno (Rev3) - ICSP
  Part4 = NRF24L01+ Breakout Board
  S1 = H-Bridge with L298N
  M1 = DC Motor
  M2 = DC Motor
  VCC1 = Battery

nets:
  N1: Part3.ICSP_MOSI, Part3.D11_PWM/MOSI, Part4.MOSI
  N2: Part3.D9_PWM, Part4.CE
  N3: Part3.D10_PWM/SS, Part4.CS
  N4: Part3.D12/MISO, Part4.MISO
  N5: Part3.D13/SCK, Part4.SCK
  N6: Part3.D2, S1.IN1
  N7: Part3.D3_PWM, S1.IN2
  N8: Part3.D4, S1.IN3
  N9: Part3.D5_PWM, S1.IN4
  3V3: Part3.3V3, Part4.VCC
  N10: Part3.5V, S1.ENA, S1.ENB
  GND: Part3.GND, Part4.GND, S1.GND, VCC1.-
  VIN: Part3.VIN, S1.5V
  N11: S1.12V, VCC1.+
  N12: S1.M1-01, M1.pin_2
  N13: S1.M1-02, M1.pin_1
  N14: S1.M2-01, M2.pin_2
  N15: S1.M2-02, M2.pin_1

custom parts:
  H-Bridge with L298N: h-bridge
  Battery: Your standard 2x 18650 battery pack (7,4 Volts)
