# Fritzing sketch transmittercircuit (saved by Fritzing 0.9.3b)
breadboards: 1

parts:
  Part1 = Arduino Uno (Rev3) - ICSP
  GY1 = MPU-6050 Board GY-521 [form="♀ (female)" package=THT]
  Part2 = NRF24L01+ Breakout Board

nets:
  N1: Part1.A4/SDA, GY1.pin4, GY1.pin5
  N2: Part1.A5/SCL, GY1.pin3
  N3: Part1.ICSP_MOSI, Part1.D11_PWM/MOSI, Part2.MOSI
  N4: Part1.D9_PWM, Part2.CE
  N5: Part1.D10_PWM/SS, Part2.CS
  N6: Part1.D12/MISO, Part2.MISO
  N7: Part1.D13/SCK, Part2.SCK
  3V3: Part1.3V3, GY1.pin1, Part2.VCC
  GND: Part1.GND, GY1.pin2, Part2.GND

custom parts:
  MPU-6050 Board GY-521: Acelerometro y Giroscopio MPU-6050 Board GY-521

// code stored in the sketch: Untitled2.ino
#include <nRF24L01.h>
#include <printf.h>
#include <RF24.h>
#include <RF24_config.h>
#include <Wire.h>
#include <MPU6050.h>
#include<SPI.h>
//mpu
MPU6050 mpu;
int16_t ax, ay, az;
int16_t gx, gy, gz;
//nrf
RF24 radio(9,10);//ce,csn
const byte address[6]="00001";

void setup() {
  // put your setup code here, to run once:
Serial.begin(9600);
radio.begin();
radio.openWritingPipe(address);
radio.stopListening();
Serial.println ("Initializing MPU and testing connections");
mpu.initialize ( );
Serial.println((mpu.testConnection( )) ? "Successfully Connected" : "Connection failed");
}

void loop() {
  // put your main code here, to run repeatedly:
  int data ;
  /*stop =1
   * right =2
   * left =3
   * back=4
   * front=5
   */
mpu.getMotion6(&ax, &ay, &az, &gx, &gy, &gz);
ax = map(ax, -17000, 17000, -125, 125);
ay = map(ay, -17000, 17000, -125, 125);
az = map(az, -17000, 17000, -125, 125);

if (ax>50){
  Serial.println("right");
  data=2;
  radio.write(&data,sizeof(data));
   delay(1000);
 
}
if (ax<-50){
  Serial.println("left");
   data=3;
  radio.write(&data,sizeof(data));
    delay(1000);

  
}
if (ax<50&&ax>-50&&ay<50&&ay>-50){
  Serial.println("stop");
   data=1;
  radio.write(&data,sizeof(data));
    delay(1000);

  
}
if (ay>50){
  Serial.println("front");  
   data=5;
  radio.write(&data,sizeof(data));
  delay(1000);

  
}
if (ay<-50){
  Serial.println("back"); 
  data=4;
  radio.write(&data,sizeof(data));
  delay(1000);

  
}


}
